# Fritzing sketch Programming circuit diagram (saved by Fritzing 0.9.3b)
breadboards: 1

parts:
  Raspberry_Pi_1 = Raspberry Pi 3 [part_number=RPI-3-V1.2]
  IC1 = L293D [package=THT]
  IC2 = L293D [package=THT]
  M1 = DC Motor
  M2 = DC Motor  # not connected
  M3 = DC Motor  # not connected
  M4 = DC Motor  # not connected
  IC3 = MCP23017 I2C I/O Expander
  LED1 = LED - 5mm [color="White (4500K)" package="5 mm [THT]"]
  LED3 = LED - 5mm [color="White (4500K)" package="5 mm [THT]"]
  Q1 = TRANSISTOR_NPN [package=to-92-ammo]
  Part1 = 9 Degrees of Freedom - Sensor Stick  # not connected
  Part2 = 9 Degrees of Freedom - Sensor Stick  # not connected
  Part3 = 9 Degrees of Freedom - Sensor Stick  # not connected
  Part4 = 9 Degrees of Freedom - Sensor Stick  # not connected
  Part5 = 9 Degrees of Freedom - Sensor Stick  # not connected
  Part6 = 9 Degrees of Freedom - Sensor Stick  # not connected
  Part7 = 9 Degrees of Freedom - Sensor Stick  # not connected
  Part8 = 9 Degrees of Freedom - Sensor Stick  # not connected
  Part9 = 9 Degrees of Freedom - Sensor Stick  # not connected
  Part10 = 9 Degrees of Freedom - Sensor Stick  # not connected
  S1 = Round Pushbutton
  S2 = Round Pushbutton
  VCC1 = Battery  # not connected
  U1 = Voltage Regulator - 5V [package="TO220 [THT]"]  # not connected

nets:
  N1: Raspberry_Pi_1.3v3, IC3.RESET
  N2: Raspberry_Pi_1.GPIO2, IC3.SDA
  N3: Raspberry_Pi_1.GPIO3, IC3.SCL
  N4: Raspberry_Pi_1.GIPO10, IC2.Enable_1
  N5: Raspberry_Pi_1.GIPO9, IC2.Enable_2
  N6: Raspberry_Pi_1.GIPO11, S2.leg1
  N7: Raspberry_Pi_1.GIPO5, IC1.In_4
  N8: Raspberry_Pi_1.GIPO6, IC1.In_3
  N9: Raspberry_Pi_1.GIPO13, IC1.In_1
  N10: Raspberry_Pi_1.GIPO19, IC1.In_2
  N11: Raspberry_Pi_1.GIPO26, IC2.In_1
  N12: Raspberry_Pi_1.GIPO21, IC2.In_2
  N13: Raspberry_Pi_1.GIPO20, IC2.In_3
  N14: Raspberry_Pi_1.GIPO16, IC2.In_4
  GND: Raspberry_Pi_1.GND, IC1.0V, IC2.0V, M1.pin_2, IC3.VSS, IC3.A0
  N15: Raspberry_Pi_1.GIPO24, IC1.Enable_2
  N16: Raspberry_Pi_1.GIPO23, IC1.Enable_1
  N17: Raspberry_Pi_1.GIPO18, S1.leg1
  N18: Raspberry_Pi_1.5V, IC2.+V
  N19: IC3.GPA7, Q1.B
  N20: LED1.cathode, LED3.anode
  N21: LED3.cathode, Q1.E

notes:
  12V DC
  1 2 3 4 5 6
  M+ M- VCC GND CH A CH B
  MCP23017 pins A0-A2 are grounded as they create the reference number for the chip which in this case is chip #0
  These are the 12V LEDs that light up things for the camera
  One set of these must be removed, we must decide on how to connect the encoders.
  VCC
  GND
  SCL
  SDA
  G
  Y EDA
  R
  O ECL
  ADO
  INT
  NCS
  FSYNC
  START BTN
  STOP BTN

custom parts:
  MCP23017 I2C I/O Expander: The MCP23017 uses two i2c pins (these can be shared with other i2c devices), and in exchange gives you 16 general purpose pins. You can set each of 16 pins to be input, output, input with a pullup or open drain. There's even the ability to get an interrupt via an external pin when any of the inputs change so you don't have to keep polling the chip.
